# Fritzing sketch principal (saved by Fritzing 0.9.3b)
circuit board: 19.4692cm x 9.17814cm
breadboards: 1

parts:
  Rasp = Raspberry Pi Zero  # not connected
  J10 = female pin header, 13 pins [form="♀ (female)"]  # not connected
  J11 = female pin header, 12 pins [form="♀ (female)"]
  P4B = Power Jack [package=power_jack_slot]
  Part1 = 16-Channel 12-bit PCA9685 PWM/Servo Driver  # not connected
  P4F = Power Jack [package=power_jack_slot]
  P4E = Power Jack [package=power_jack_slot]
  Flip_Flop = PICAXE-14M [package=THT]  # not connected
  NOT = PICAXE-14M [package=THT]  # not connected
  P4F1 = Power Jack [package=power_jack_slot]  # not connected
  P4F2 = Power Jack [package=power_jack_slot]  # not connected
  U1 = RJ45 Jack [package=rj45-8]  # not connected

nets:
  N1: J11.pin1, J11.pin2, P4E.PWR
  N2: J11.pin3, J11.pin4, P4E.GNDBREAK
  N3: J11.pin5, J11.pin6, P4B.PWR
  N4: J11.pin7, J11.pin8, P4B.GNDBREAK
  N5: J11.pin9, J11.pin10, P4F.GNDBREAK
  N6: J11.pin11, J11.pin12, P4F.PWR

custom parts:
  16-Channel 12-bit PCA9685 PWM/Servo Driver: The Adafruit 16-Channel 12-bit PWM/Servo Driver will drive up to 16 servos over I2C with only 2 pins. The on-board PCA9685 PWM controller will drive all 16 channels simultaneously with no additional processing overhead. What's more, you can chain up to 62 of them to control up to 992 servos - all with the same 2 pins
